// Logisim project ALU_v1.5.circ as structural Verilog: 27 circuits, main circuit Alu
module Alu (
  input  [7:0] N,
  input  [7:0] R0,
  input  [7:0] R1,
  input  [3:0] Banderas,
  input  [4:0] Instrucciones,
  output [7:0] ACC,
  output [7:0] ACC2,
  output [3:0] BanderasOut
);

  wire [19:0] adc_1_salida, add_1_salida, and2_1_salida, cbw_1_salida, dec_1_salida, idiv_1_salida,
       imul_1_salida, inc_1_salida, neg_1_salida, not2_1_out_2, or2_1_salida, rcl_1_salida, rcr_1_salida,
       roln_1_salida, rorn_1_salida, sal_1_out_2, sar_1_out_2, sbb_1_salida, shl_1_salida, shr_1_salida,
       sub_1_salida, xchg_1_salida, xor2_1_salida;

  XCHG xchg_1 (.Entrada({Banderas, R1, R0, N}), .Salida(xchg_1_salida));
  CBW cbw_1 (.Entrada({Banderas, R1, R0, N}), .Salida(cbw_1_salida));
  ADD add_1 (.Entrada({Banderas, R1, R0, N}), .Salida(add_1_salida));
  ADC adc_1 (.Entrada({Banderas, R1, R0, N}), .Salida(adc_1_salida));
  SUB sub_1 (.Entrada({Banderas, R1, R0, N}), .Salida(sub_1_salida));
  SBB sbb_1 (.Entrada({Banderas, R1, R0, N}), .Salida(sbb_1_salida));
  IDIV idiv_1 (.ENTRADA({Banderas, R1, R0, N}), .SALIDA(idiv_1_salida));
  IMUL imul_1 (.in_1({Banderas, R1, R0, N}), .salida(imul_1_salida));
  INC inc_1 (.Entrada({Banderas, R1, R0, N}), .Salida(inc_1_salida));
  DEC dec_1 (.Entrada({Banderas, R1, R0, N}), .Salida(dec_1_salida));
  NEG neg_1 (.Entrada({Banderas, R1, R0, N}), .Salida(neg_1_salida));
  SAL sal_1 (.in_1({Banderas, R1, R0, N}), .out_2(sal_1_out_2));
  SAR sar_1 (.in_1({Banderas, R1, R0, N}), .out_2(sar_1_out_2));
  NOT2 not2_1 (.in_1({Banderas, R1, R0, N}), .out_2(not2_1_out_2));
  AND2 and2_1 (.Entrada({Banderas, R1, R0, N}), .Salida(and2_1_salida));
  OR2 or2_1 (.Entrada({Banderas, R1, R0, N}), .Salida(or2_1_salida));
  XOR2 xor2_1 (.Entrada({Banderas, R1, R0, N}), .Salida(xor2_1_salida));
  SHL shl_1 (.ENTRADA({Banderas, R1, R0, N}), .SALIDA(shl_1_salida));
  SHR shr_1 (.ENTRADA({Banderas, R1, R0, N}), .SALIDA(shr_1_salida));
  RCL rcl_1 (.Entrada({Banderas, R1, R0, N}), .SALIDA(rcl_1_salida));
  RCR rcr_1 (.Entrada({Banderas, R1, R0, N}), .SALIDA(rcr_1_salida));
  ROLN roln_1 (.ENTRADA({Banderas, R1, R0, N}), .SALIDA(roln_1_salida));
  RORN rorn_1 (.ENTRADA({Banderas, R1, R0, N}), .SALIDA(rorn_1_salida));
  Multiplexer #(.select(5), .width(20)) multiplexer_1 (
    .in0(xchg_1_salida), .in1(cbw_1_salida), .in2(add_1_salida), .in3(adc_1_salida), .in4(sub_1_salida),
    .in5(sbb_1_salida), .in6(idiv_1_salida), .in7(imul_1_salida), .in8(inc_1_salida), .in9(dec_1_salida),
    .in10(neg_1_salida), .in11(sal_1_out_2), .in12(sar_1_out_2), .in13(not2_1_out_2), .in14(and2_1_salida),
    .in15(or2_1_salida), .in16(xor2_1_salida), .in17(shl_1_salida), .in18(shr_1_salida), .in19(rcl_1_salida),
    .in20(rcr_1_salida), .in21(roln_1_salida), .in22(rorn_1_salida), .out({BanderasOut, ACC2, ACC}),
    .sel(Instrucciones));  // open: in23, in24, in25, in26, in27, in28, in29, in30, in31

  // Notes on the sheet:
  //   C O S Z
endmodule

module XCHG (
  input  [27:0] Entrada,
  output [19:0] Salida
);


  assign Salida = {Entrada[27:24], Entrada[15:8], Entrada[23:16]};

  // Notes on the sheet:
  //   N
  //   BANDERAS
  //   R0 -> ACC2
  //   R1 -> ACC
endmodule

module CBW (
  input  [27:0] Entrada,
  output [19:0] Salida
);

  nor nor_1 (Salida[16], Entrada[6], Entrada[0], Entrada[1], Entrada[2], Entrada[3], Entrada[4], Entrada[5], Entrada[7]);

  assign {Salida[19:17], Salida[15:0]} = {Entrada[25:24], {10{Entrada[7]}}, Entrada[6:0]};

  // Notes on the sheet:
  //   Entrada: initial=0x33
endmodule

module ADD (
  input  [27:0] Entrada,
  output [19:0] Salida
);

  wire xnor_1_out, xor_1_out;

  Adder adder_1 (.a(Entrada[7:0]), .b(Entrada[15:8]), .out({Salida[17], Salida[6:0]}), .cin(1'b0), .cout(Salida[19]));
  xor xor_1 (xor_1_out, Salida[17], Entrada[7]);
  xnor xnor_1 (xnor_1_out, Entrada[7], Entrada[15]);
  nor nor_1 (Salida[16], Salida[0], Salida[1], Salida[2], Salida[3], Salida[4], Salida[5], Salida[6], Salida[17]);
  and and_1 (Salida[18], xor_1_out, xnor_1_out);

  assign Salida[15:7] = {Entrada[23:16], Salida[17]};

  // Notes on the sheet:
  //   N
  //   R0
  //   R1
  //   acc
  //   acc2
  //   cosz
endmodule

module ADC (
  input  [27:0] Entrada,
  output [19:0] Salida
);

  wire xnor_1_out, xor_1_out;

  Adder adder_1 (
    .a(Entrada[7:0]), .b(Entrada[15:8]), .out({Salida[17], Salida[6:0]}), .cin(Entrada[27]), .cout(Salida[19]));
  xor xor_1 (xor_1_out, Salida[17], Entrada[7]);
  xnor xnor_1 (xnor_1_out, Entrada[7], Entrada[15]);
  nor nor_1 (Salida[16], Salida[0], Salida[1], Salida[2], Salida[3], Salida[4], Salida[5], Salida[6], Salida[17]);
  and and_1 (Salida[18], xor_1_out, xnor_1_out);

  assign Salida[15:7] = {Entrada[23:16], Salida[17]};

  // Notes on the sheet:
  //   N
  //   R0
  //   R1
  //   acc
  //   acc2
  //   cosz
endmodule

module SUB (
  input  [27:0] Entrada,
  output [19:0] Salida
);

  wire and_1_out, and_2_out, comparator_1_gt, comparator_1_lt, comparator_2_gt, comparator_2_lt,
       comparator_3_gt, comparator_3_lt;

  Subtractor subtractor_1 (
    .a(Entrada[15:8]), .b(Entrada[7:0]), .out({Salida[17], Salida[6:0]}), .bin(1'b0), .bout(Salida[19]));
  nor nor_1 (Salida[16], Salida[0], Salida[1], Salida[2], Salida[3], Salida[4], Salida[5], Salida[6], Salida[17]);
  Comparator comparator_1 (
    .a({Salida[17], Salida[6:0]}), .b({8{1'b0}}), .gt(comparator_1_gt), .lt(comparator_1_lt));  // open: eq
  Comparator comparator_2 (.a(Entrada[7:0]), .b({8{1'b0}}), .gt(comparator_2_gt), .lt(comparator_2_lt));  // open: eq
  Comparator comparator_3 (.a(Entrada[15:8]), .b({8{1'b0}}), .gt(comparator_3_gt), .lt(comparator_3_lt));  // open: eq
  and and_1 (and_1_out, comparator_1_lt, comparator_2_gt, comparator_3_lt);
  and and_2 (and_2_out, comparator_1_gt, comparator_2_lt, comparator_3_gt);
  or or_1 (Salida[18], and_1_out, and_2_out);

  assign Salida[15:7] = {Entrada[23:16], Salida[17]};

  // Notes on the sheet:
  //   N
  //   R0
  //   R1
  //   acc
  //   acc2
  //   t
  //   b
  //   a
  //   cosz
endmodule

module SBB (
  input  [27:0] Entrada,
  output [19:0] Salida
);

  wire and_1_out, and_2_out, comparator_1_gt, comparator_1_lt, comparator_2_gt, comparator_2_lt,
       comparator_3_gt, comparator_3_lt;

  Subtractor subtractor_1 (
    .a(Entrada[15:8]), .b(Entrada[7:0]), .out({Salida[17], Salida[6:0]}), .bin(Entrada[27]), .bout(Salida[19]));
  nor nor_1 (Salida[16], Salida[0], Salida[1], Salida[2], Salida[3], Salida[4], Salida[5], Salida[6], Salida[17]);
  Comparator comparator_1 (
    .a({Salida[17], Salida[6:0]}), .b({8{1'b0}}), .gt(comparator_1_gt), .lt(comparator_1_lt));  // open: eq
  Comparator comparator_2 (.a(Entrada[7:0]), .b({8{1'b0}}), .gt(comparator_2_gt), .lt(comparator_2_lt));  // open: eq
  Comparator comparator_3 (.a(Entrada[15:8]), .b({8{1'b0}}), .gt(comparator_3_gt), .lt(comparator_3_lt));  // open: eq
  and and_1 (and_1_out, comparator_1_lt, comparator_2_gt, comparator_3_lt);
  and and_2 (and_2_out, comparator_1_gt, comparator_2_lt, comparator_3_gt);
  or or_1 (Salida[18], and_1_out, and_2_out);

  assign Salida[15:7] = {Entrada[23:16], Salida[17]};

  // Notes on the sheet:
  //   N
  //   R0
  //   R1
  //   acc
  //   acc2
  //   t
  //   b
  //   a
  //   cosz
endmodule

module IDIV (
  input  [27:0] ENTRADA,
  output [19:0] SALIDA
);

  IDIV_div8b idiv_div8b_1 (
    .Divisor(ENTRADA[7:0]), .Dividendo(ENTRADA[23:8]), .CocienteOut({SALIDA[17], SALIDA[6:0]}),
    .ResiduoOut(SALIDA[15:8]));  // open: Overflow, Oout, DivisorOut, DividendoOut, Cout, Sout, Zout
  Comparator comparator_1 (.a({SALIDA[17], SALIDA[6:0]}), .b({8{1'b0}}), .eq(SALIDA[16]));  // open: gt, lt

  assign {SALIDA[19:18], SALIDA[7]} = {ENTRADA[27:26], SALIDA[17]};
endmodule

module IMUL (
  input  [27:0] in_1,
  output [19:0] salida
);

  wire [15:0] multiplicador8bitmini_1_asalida, multiplicador8bitmini_1_bsalida,
       multiplicador8bitmini_1_csalida, multiplicador8bitmini_2_asalida, multiplicador8bitmini_2_bsalida,
       multiplicador8bitmini_2_csalida, multiplicador8bitmini_3_asalida, multiplicador8bitmini_3_bsalida,
       multiplicador8bitmini_3_csalida, multiplicador8bitmini_4_asalida, multiplicador8bitmini_4_bsalida,
       multiplicador8bitmini_4_csalida, multiplicador8bitmini_5_asalida, multiplicador8bitmini_5_bsalida,
       multiplicador8bitmini_5_csalida, multiplicador8bitmini_6_asalida, multiplicador8bitmini_6_bsalida,
       multiplicador8bitmini_6_csalida, multiplicador8bitmini_7_asalida, multiplicador8bitmini_7_bsalida,
       multiplicador8bitmini_7_csalida;

  nor nor_1 (salida[16], salida[0], salida[1], salida[2], salida[3], salida[4], salida[5], salida[6], salida[7], salida[8], salida[9], salida[10], salida[11], salida[12], salida[13], salida[14], salida[17]);
  multiplicador8bitmini multiplicador8bitmini_1 (
    .A({{9{in_1[7]}}, in_1[6:0]}), .B({{9{in_1[15]}}, in_1[14:8]}), .C({16{1'b0}}),
    .Asalida(multiplicador8bitmini_1_asalida), .Bsalida(multiplicador8bitmini_1_bsalida),
    .Csalida(multiplicador8bitmini_1_csalida));
  multiplicador8bitmini multiplicador8bitmini_2 (
    .A(multiplicador8bitmini_7_asalida), .B(multiplicador8bitmini_7_bsalida),
    .C(multiplicador8bitmini_7_csalida), .Asalida(multiplicador8bitmini_2_asalida),
    .Bsalida(multiplicador8bitmini_2_bsalida), .Csalida(multiplicador8bitmini_2_csalida));
  multiplicador8bitmini multiplicador8bitmini_3 (
    .A(multiplicador8bitmini_1_asalida), .B(multiplicador8bitmini_1_bsalida),
    .C(multiplicador8bitmini_1_csalida), .Asalida(multiplicador8bitmini_3_asalida),
    .Bsalida(multiplicador8bitmini_3_bsalida), .Csalida(multiplicador8bitmini_3_csalida));
  multiplicador8bitmini multiplicador8bitmini_4 (
    .A(multiplicador8bitmini_2_asalida), .B(multiplicador8bitmini_2_bsalida),
    .C(multiplicador8bitmini_2_csalida), .Asalida(multiplicador8bitmini_4_asalida),
    .Bsalida(multiplicador8bitmini_4_bsalida), .Csalida(multiplicador8bitmini_4_csalida));
  multiplicador8bitmini multiplicador8bitmini_5 (
    .A(multiplicador8bitmini_3_asalida), .B(multiplicador8bitmini_3_bsalida),
    .C(multiplicador8bitmini_3_csalida), .Asalida(multiplicador8bitmini_5_asalida),
    .Bsalida(multiplicador8bitmini_5_bsalida), .Csalida(multiplicador8bitmini_5_csalida));
  multiplicador8bitmini multiplicador8bitmini_6 (
    .A(multiplicador8bitmini_4_asalida), .B(multiplicador8bitmini_4_bsalida),
    .C(multiplicador8bitmini_4_csalida), .Asalida(multiplicador8bitmini_6_asalida),
    .Bsalida(multiplicador8bitmini_6_bsalida), .Csalida(multiplicador8bitmini_6_csalida));
  multiplicador8bitmini multiplicador8bitmini_7 (
    .A(multiplicador8bitmini_5_asalida), .B(multiplicador8bitmini_5_bsalida),
    .C(multiplicador8bitmini_5_csalida), .Asalida(multiplicador8bitmini_7_asalida),
    .Bsalida(multiplicador8bitmini_7_bsalida), .Csalida(multiplicador8bitmini_7_csalida));
  multiplicador8bitmini multiplicador8bitmini_8 (
    .A(multiplicador8bitmini_6_asalida), .B(multiplicador8bitmini_6_bsalida),
    .C(multiplicador8bitmini_6_csalida), .Csalida({salida[17], salida[14:0]}));  // open: Asalida, Bsalida

  assign {salida[19:18], salida[15]} = {in_1[24], in_1[25], salida[17]};
endmodule

module INC (
  input  [27:0] Entrada,
  output [19:0] Salida
);

  wire xnor_1_out, xor_1_out;

  Adder adder_1 (.a(Entrada[7:0]), .b(8'h1), .out({Salida[17], Salida[6:0]}), .cin(1'b0), .cout(Salida[19]));
  xor xor_1 (xor_1_out, Salida[17], Entrada[7]);
  xnor xnor_1 (xnor_1_out, Entrada[7], 1'b0);
  nor nor_1 (Salida[16], Salida[0], Salida[1], Salida[2], Salida[3], Salida[4], Salida[5], Salida[6], Salida[17]);
  and and_1 (Salida[18], xor_1_out, xnor_1_out);

  assign Salida[15:7] = {Entrada[23:16], Salida[17]};

  // Notes on the sheet:
  //   N
  //   R0
  //   R1
  //   Z
  //   S
  //   O
  //   C
endmodule

module DEC (
  input  [27:0] Entrada,
  output [19:0] Salida
);

  wire xnor_1_out;

  Subtractor subtractor_1 (.a(Entrada[7:0]), .b(8'h1), .out({Salida[17], Salida[6:0]}), .bin(1'b0), .bout(Salida[19]));
  xnor xnor_1 (xnor_1_out, Entrada[7], 1'b0);
  // XOR_Gate xor_1 is placed but not wired
  nor nor_1 (Salida[16], Salida[0], Salida[1], Salida[2], Salida[3], Salida[4], Salida[5], Salida[6], Salida[17]);
  and and_1 (Salida[18], Entrada[7], xnor_1_out);

  assign Salida[15:7] = {Entrada[23:16], Salida[17]};

  // Notes on the sheet:
  //   N
  //   R0
  //   R1
  //   Z
  //   S
  //   O
  //   C
endmodule

module NEG (
  input  [27:0] Entrada,
  output [19:0] Salida
);

  wire [7:0] adder_1_out;

  assign Salida[7:0] = ~adder_1_out;  // NOT_Gate not_1, 8 bits wide
  Adder adder_1 (.a({8{1'b1}}), .b(Entrada[7:0]), .out(adder_1_out), .cout(Salida[16]));  // open: cin
  nor nor_1 (Salida[19], Entrada[0], Entrada[1], Entrada[2], Entrada[3], Entrada[4], Entrada[5], Entrada[6], Entrada[7]);

  assign {Salida[18:17], Salida[15:8]} = {Entrada[7], Entrada[24:16]};

  // Notes on the sheet:
  //   COSZ
endmodule

module SAL (
  input  [27:0] in_1,
  output [19:0] out_2
);

  xor xor_1 (out_2[18], in_1[6], in_1[7]);
  nor nor_1 (out_2[16], 1'b0, in_1[0], in_1[1], in_1[2], in_1[3], in_1[4], in_1[5], in_1[6]);

  assign {out_2[19], out_2[17], out_2[15:0]} = {in_1[7:6], in_1[23:16], in_1[6:0], 1'b0};

  // Notes on the sheet:
  //   COSZ
endmodule

module SAR (
  input  [27:0] in_1,
  output [19:0] out_2
);

  nor nor_1 (out_2[16], in_1[1], in_1[2], in_1[3], in_1[4], in_1[5], in_1[6], in_1[7], in_1[7]);

  assign {out_2[19:17], out_2[15:0]} = {in_1[0], 1'b0, in_1[7], in_1[23:16], {2{in_1[7]}}, in_1[6:1]};

  // Notes on the sheet:
  //   COSZ
endmodule

module NOT2 (
  input  [27:0] in_1,
  output [19:0] out_2
);

  assign {out_2[17], out_2[6:0]} = ~in_1[7:0];  // NOT_Gate not_1, 8 bits wide
  nor nor_1 (out_2[16], out_2[0], out_2[1], out_2[2], out_2[3], out_2[4], out_2[5], out_2[6], out_2[17]);

  assign {out_2[19:18], out_2[15:7]} = {in_1[24], in_1[25], in_1[23:16], out_2[17]};

  // Notes on the sheet:
  //   COSZ
endmodule

module AND2 (
  input  [27:0] Entrada,
  output [19:0] Salida
);

  assign {Salida[17], Salida[6:0]} = Entrada[7:0] & Entrada[15:8];  // AND_Gate and_1, 8 bits wide
  nor nor_1 (Salida[16], Salida[0], Salida[1], Salida[2], Salida[3], Salida[4], Salida[5], Salida[6], Salida[17]);

  assign {Salida[19:18], Salida[15:7]} = {Entrada[24], Entrada[25], Entrada[23:16], Salida[17]};
endmodule

module OR2 (
  input  [27:0] Entrada,
  output [19:0] Salida
);

  assign {Salida[17], Salida[6:0]} = Entrada[7:0] | Entrada[15:8];  // OR_Gate or_1, 8 bits wide
  nor nor_1 (Salida[16], Salida[0], Salida[1], Salida[2], Salida[3], Salida[4], Salida[5], Salida[6], Salida[17]);

  assign {Salida[19:18], Salida[15:7]} = {Entrada[24], Entrada[25], Entrada[23:16], Salida[17]};
endmodule

module XOR2 (
  input  [27:0] Entrada,
  output [19:0] Salida
);

  assign {Salida[17], Salida[6:0]} = Entrada[7:0] ^ Entrada[15:8];  // XOR_Gate xor_1, 8 bits wide
  nor nor_1 (Salida[16], Salida[0], Salida[1], Salida[2], Salida[3], Salida[4], Salida[5], Salida[6], Salida[17]);

  assign {Salida[19:18], Salida[15:7]} = {Entrada[24], Entrada[25], Entrada[23:16], Salida[17]};
endmodule

module SHL (
  input  [27:0] ENTRADA,
  output [19:0] SALIDA
);

  Comparator comparator_1 (.a({ENTRADA[6:0], 1'b0}), .b({8{1'b0}}), .eq(SALIDA[16]));  // open: gt, lt

  assign {SALIDA[19:17], SALIDA[15:0]} = {ENTRADA[7], ENTRADA[26], ENTRADA[6], ENTRADA[23:16], ENTRADA[6:0], 1'b0};
endmodule

module SHR (
  input  [27:0] ENTRADA,
  output [19:0] SALIDA
);

  Comparator comparator_1 (.a({1'b0, ENTRADA[7:1]}), .b({8{1'b0}}), .eq(SALIDA[16]));  // open: gt, lt

  assign {SALIDA[19:17], SALIDA[15:0]} = {ENTRADA[0], ENTRADA[26], 1'b0, ENTRADA[23:16], 1'b0, ENTRADA[7:1]};
endmodule

module RCL (
  input  [27:0] Entrada,
  output [19:0] SALIDA
);

  Comparator comparator_1 (.a({Entrada[6:0], Entrada[24]}), .b({8{1'b0}}), .eq(SALIDA[16]));  // open: gt, lt

  assign {SALIDA[19:17], SALIDA[15:0]} = {Entrada[7], Entrada[26], Entrada[6], Entrada[23:16], Entrada[6:0], Entrada[24]};
endmodule

module RCR (
  input  [27:0] Entrada,
  output [19:0] SALIDA
);

  Comparator comparator_1 (.a({Entrada[24], Entrada[7:1]}), .b({8{1'b0}}), .eq(SALIDA[16]));  // open: gt, lt

  assign {SALIDA[19:17], SALIDA[15:0]} = {Entrada[0], Entrada[26], Entrada[24:16], Entrada[24], Entrada[7:1]};
endmodule

module ROLN (
  input  [27:0] ENTRADA,
  output [19:0] SALIDA
);

  Comparator comparator_1 (.a({ENTRADA[6:0], ENTRADA[7]}), .b({8{1'b0}}), .eq(SALIDA[16]));  // open: gt, lt

  assign {SALIDA[19:17], SALIDA[15:0]} = {ENTRADA[7], ENTRADA[26], ENTRADA[6], ENTRADA[23:16], ENTRADA[6:0], ENTRADA[7]};
endmodule

module RORN (
  input  [27:0] ENTRADA,
  output [19:0] SALIDA
);

  Comparator comparator_1 (.a({ENTRADA[0], ENTRADA[7:1]}), .b({8{1'b0}}), .eq(SALIDA[16]));  // open: gt, lt

  assign {SALIDA[19:17], SALIDA[15:0]} = {ENTRADA[0], ENTRADA[26], ENTRADA[0], ENTRADA[23:16], ENTRADA[0], ENTRADA[7:1]};
endmodule

module multiplicador8bitmini (
  input  [15:0] A,
  input  [15:0] B,
  input  [15:0] C,
  output [15:0] Asalida,
  output [15:0] Bsalida,
  output [15:0] Csalida
);

  wire adder_1_cout;
  wire [15:0] multiplexer_1_out;

  Multiplexer #(.width(16)) multiplexer_1 (.in0({16{1'b0}}), .in1(A), .out(multiplexer_1_out), .sel(B[0]));
  Adder #(.width(16)) adder_1 (.a(multiplexer_1_out), .b(C), .out(Csalida), .cin(1'b0), .cout(adder_1_cout));

  assign Asalida = {A[14:0], 1'b0};
  assign Bsalida = {1'b0, B[15:1]};
endmodule

module IDIV_div8b (
  input  [7:0] Divisor,
  input  [15:0] Dividendo,
  output Overflow,
  output [7:0] CocienteOut,
  output [7:0] ResiduoOut,
  output Oout,
  output [7:0] DivisorOut,
  output [15:0] DividendoOut,
  output Cout,
  output Sout,
  output Zout
);

  wire [7:0] divicionetapa1_1_cocienteout, divicionetapa1_1_divisorout, divicionetapa1_1_residuoout,
       divicionetapa1_2_cocienteout, divicionetapa1_2_divisorout, divicionetapa1_2_residuoout,
       divicionetapa1_3_cocienteout, divicionetapa1_3_divisorout, divicionetapa1_3_residuoout,
       divicionetapa1_4_cocienteout, divicionetapa1_4_divisorout, divicionetapa1_4_residuoout,
       divicionetapa1_5_cocienteout, divicionetapa1_5_divisorout, divicionetapa1_5_residuoout,
       divicionetapa1_6_cocienteout, divicionetapa1_6_divisorout, divicionetapa1_6_residuoout,
       divicionetapa1_7_cocienteout, divicionetapa1_7_divisorout, divicionetapa1_7_residuoout,
       divicionetapa1_8_cocienteout, divicionetapa1_8_divisorout, divicionetapa1_8_residuoout,
       divicionetapa1_9_cocienteout, divicionetapa1_9_divisorout, divicionetapa1_9_residuoout,
       divicionetapa1_10_cocienteout, divicionetapa1_10_divisorout, divicionetapa1_10_residuoout,
       divicionetapa1_11_cocienteout, divicionetapa1_11_divisorout, divicionetapa1_11_residuoout,
       divicionetapa1_12_cocienteout, divicionetapa1_12_divisorout, divicionetapa1_12_residuoout,
       divicionetapa1_13_cocienteout, divicionetapa1_13_divisorout, divicionetapa1_13_residuoout,
       divicionetapa1_14_cocienteout, divicionetapa1_14_divisorout, divicionetapa1_14_residuoout,
       divicionetapa1_16_cocienteout, divicionetapa1_16_divisorout, divicionetapa1_16_residuoout;
  wire [15:0] divicionetapa1_1_dividendoout, divicionetapa1_2_dividendoout, divicionetapa1_3_dividendoout,
       divicionetapa1_4_dividendoout, divicionetapa1_5_dividendoout, divicionetapa1_6_dividendoout,
       divicionetapa1_7_dividendoout, divicionetapa1_8_dividendoout, divicionetapa1_9_dividendoout,
       divicionetapa1_10_dividendoout, divicionetapa1_11_dividendoout, divicionetapa1_12_dividendoout,
       divicionetapa1_13_dividendoout, divicionetapa1_14_dividendoout, divicionetapa1_16_dividendoout;

  divicionEtapa1 divicionetapa1_1 (
    .Cociente({8{1'b0}}), .Residuo({8{1'b0}}), .Divisor(Divisor), .Dividendo(Dividendo),
    .CocienteOut(divicionetapa1_1_cocienteout), .ResiduoOut(divicionetapa1_1_residuoout),
    .DivisorOut(divicionetapa1_1_divisorout), .DividendoOut(divicionetapa1_1_dividendoout));
  divicionEtapa1 divicionetapa1_2 (
    .Cociente(divicionetapa1_16_cocienteout), .Residuo(divicionetapa1_16_residuoout),
    .Divisor(divicionetapa1_16_divisorout), .Dividendo(divicionetapa1_16_dividendoout),
    .CocienteOut(divicionetapa1_2_cocienteout), .ResiduoOut(divicionetapa1_2_residuoout),
    .DivisorOut(divicionetapa1_2_divisorout), .DividendoOut(divicionetapa1_2_dividendoout));
  divicionEtapa1 divicionetapa1_3 (
    .Cociente(divicionetapa1_13_cocienteout), .Residuo(divicionetapa1_13_residuoout),
    .Divisor(divicionetapa1_13_divisorout), .Dividendo(divicionetapa1_13_dividendoout),
    .CocienteOut(divicionetapa1_3_cocienteout), .ResiduoOut(divicionetapa1_3_residuoout),
    .DivisorOut(divicionetapa1_3_divisorout), .DividendoOut(divicionetapa1_3_dividendoout));
  divicionEtapa1 divicionetapa1_4 (
    .Cociente(divicionetapa1_14_cocienteout), .Residuo(divicionetapa1_14_residuoout),
    .Divisor(divicionetapa1_14_divisorout), .Dividendo(divicionetapa1_14_dividendoout),
    .CocienteOut(divicionetapa1_4_cocienteout), .ResiduoOut(divicionetapa1_4_residuoout),
    .DivisorOut(divicionetapa1_4_divisorout), .DividendoOut(divicionetapa1_4_dividendoout));
  divicionEtapa1 divicionetapa1_5 (
    .Cociente(divicionetapa1_1_cocienteout), .Residuo(divicionetapa1_1_residuoout),
    .Divisor(divicionetapa1_1_divisorout), .Dividendo(divicionetapa1_1_dividendoout),
    .CocienteOut(divicionetapa1_5_cocienteout), .ResiduoOut(divicionetapa1_5_residuoout),
    .DivisorOut(divicionetapa1_5_divisorout), .DividendoOut(divicionetapa1_5_dividendoout));
  divicionEtapa1 divicionetapa1_6 (
    .Cociente(divicionetapa1_2_cocienteout), .Residuo(divicionetapa1_2_residuoout),
    .Divisor(divicionetapa1_2_divisorout), .Dividendo(divicionetapa1_2_dividendoout),
    .CocienteOut(divicionetapa1_6_cocienteout), .ResiduoOut(divicionetapa1_6_residuoout),
    .DivisorOut(divicionetapa1_6_divisorout), .DividendoOut(divicionetapa1_6_dividendoout));
  divicionEtapa1 divicionetapa1_7 (
    .Cociente(divicionetapa1_3_cocienteout), .Residuo(divicionetapa1_3_residuoout),
    .Divisor(divicionetapa1_3_divisorout), .Dividendo(divicionetapa1_3_dividendoout),
    .CocienteOut(divicionetapa1_7_cocienteout), .ResiduoOut(divicionetapa1_7_residuoout),
    .DivisorOut(divicionetapa1_7_divisorout), .DividendoOut(divicionetapa1_7_dividendoout));
  divicionEtapa1 divicionetapa1_8 (
    .Cociente(divicionetapa1_4_cocienteout), .Residuo(divicionetapa1_4_residuoout),
    .Divisor(divicionetapa1_4_divisorout), .Dividendo(divicionetapa1_4_dividendoout),
    .CocienteOut(divicionetapa1_8_cocienteout), .ResiduoOut(divicionetapa1_8_residuoout),
    .DivisorOut(divicionetapa1_8_divisorout), .DividendoOut(divicionetapa1_8_dividendoout));
  divicionEtapa1 divicionetapa1_9 (
    .Cociente(divicionetapa1_5_cocienteout), .Residuo(divicionetapa1_5_residuoout),
    .Divisor(divicionetapa1_5_divisorout), .Dividendo(divicionetapa1_5_dividendoout),
    .CocienteOut(divicionetapa1_9_cocienteout), .ResiduoOut(divicionetapa1_9_residuoout),
    .DivisorOut(divicionetapa1_9_divisorout), .DividendoOut(divicionetapa1_9_dividendoout));
  divicionEtapa1 divicionetapa1_10 (
    .Cociente(divicionetapa1_6_cocienteout), .Residuo(divicionetapa1_6_residuoout),
    .Divisor(divicionetapa1_6_divisorout), .Dividendo(divicionetapa1_6_dividendoout),
    .CocienteOut(divicionetapa1_10_cocienteout), .ResiduoOut(divicionetapa1_10_residuoout),
    .DivisorOut(divicionetapa1_10_divisorout), .DividendoOut(divicionetapa1_10_dividendoout));
  divicionEtapa1 divicionetapa1_11 (
    .Cociente(divicionetapa1_7_cocienteout), .Residuo(divicionetapa1_7_residuoout),
    .Divisor(divicionetapa1_7_divisorout), .Dividendo(divicionetapa1_7_dividendoout),
    .CocienteOut(divicionetapa1_11_cocienteout), .ResiduoOut(divicionetapa1_11_residuoout),
    .DivisorOut(divicionetapa1_11_divisorout), .DividendoOut(divicionetapa1_11_dividendoout));
  divicionEtapa1 divicionetapa1_12 (
    .Cociente(divicionetapa1_8_cocienteout), .Residuo(divicionetapa1_8_residuoout),
    .Divisor(divicionetapa1_8_divisorout), .Dividendo(divicionetapa1_8_dividendoout),
    .CocienteOut(divicionetapa1_12_cocienteout), .ResiduoOut(divicionetapa1_12_residuoout),
    .DivisorOut(divicionetapa1_12_divisorout), .DividendoOut(divicionetapa1_12_dividendoout));
  divicionEtapa1 divicionetapa1_13 (
    .Cociente(divicionetapa1_10_cocienteout), .Residuo(divicionetapa1_10_residuoout),
    .Divisor(divicionetapa1_10_divisorout), .Dividendo(divicionetapa1_10_dividendoout),
    .CocienteOut(divicionetapa1_13_cocienteout), .ResiduoOut(divicionetapa1_13_residuoout),
    .DivisorOut(divicionetapa1_13_divisorout), .DividendoOut(divicionetapa1_13_dividendoout));
  divicionEtapa1 divicionetapa1_14 (
    .Cociente(divicionetapa1_11_cocienteout), .Residuo(divicionetapa1_11_residuoout),
    .Divisor(divicionetapa1_11_divisorout), .Dividendo(divicionetapa1_11_dividendoout),
    .CocienteOut(divicionetapa1_14_cocienteout), .ResiduoOut(divicionetapa1_14_residuoout),
    .DivisorOut(divicionetapa1_14_divisorout), .DividendoOut(divicionetapa1_14_dividendoout));
  divicionEtapa1 divicionetapa1_15 (
    .Cociente(divicionetapa1_12_cocienteout), .Residuo(divicionetapa1_12_residuoout),
    .Divisor(divicionetapa1_12_divisorout), .Dividendo(divicionetapa1_12_dividendoout),
    .CocienteOut(CocienteOut), .ResiduoOut(ResiduoOut), .DivisorOut(DivisorOut), .DividendoOut(DividendoOut));
  divicionEtapa1 divicionetapa1_16 (
    .Cociente(divicionetapa1_9_cocienteout), .Residuo(divicionetapa1_9_residuoout),
    .Divisor(divicionetapa1_9_divisorout), .Dividendo(divicionetapa1_9_dividendoout),
    .CocienteOut(divicionetapa1_16_cocienteout), .ResiduoOut(divicionetapa1_16_residuoout),
    .DivisorOut(divicionetapa1_16_divisorout), .DividendoOut(divicionetapa1_16_dividendoout));
  or or_1 (Overflow, divicionetapa1_13_cocienteout[0], divicionetapa1_13_cocienteout[1], divicionetapa1_13_cocienteout[2], divicionetapa1_13_cocienteout[3], divicionetapa1_13_cocienteout[4], divicionetapa1_13_cocienteout[5], divicionetapa1_13_cocienteout[6], divicionetapa1_13_cocienteout[7]);
  nor nor_1 (Cout, DivisorOut[0], DivisorOut[1], DivisorOut[2], DivisorOut[3], DivisorOut[4], DivisorOut[5], DivisorOut[6], DivisorOut[7]);
  nor nor_2 (Zout, CocienteOut[0], CocienteOut[1], CocienteOut[2], CocienteOut[3], CocienteOut[4], CocienteOut[5], CocienteOut[6], CocienteOut[7]);
  or or_2 (Oout, Overflow, Cout);

  assign Sout = CocienteOut[7];
endmodule

module divicionEtapa1 (
  input  [7:0] Cociente,
  input  [7:0] Residuo,
  input  [7:0] Divisor,
  input  [15:0] Dividendo,
  output [7:0] CocienteOut,
  output [7:0] ResiduoOut,
  output [7:0] DivisorOut,
  output [15:0] DividendoOut
);

  wire comparator_1_eq, comparator_1_gt, or_3_out;
  wire [7:0] multiplexer_1_out, or_1_out, or_2_out, subtractor_1_out;

  assign or_1_out = {Residuo[6:0], 1'b0} | 8'h1;  // OR_Gate or_1, 8 bits wide
  Multiplexer #(.width(8)) multiplexer_1 (
    .in0({Residuo[6:0], 1'b0}), .in1(or_1_out), .out(multiplexer_1_out), .sel(Dividendo[15]));
  assign or_2_out = {Cociente[6:0], 1'b0} | 8'h1;  // OR_Gate or_2, 8 bits wide
  Subtractor subtractor_1 (.a(multiplexer_1_out), .b(Divisor), .out(subtractor_1_out), .bin(1'b0));  // open: bout
  Comparator #(.mode("unsigned")) comparator_1 (
    .a(multiplexer_1_out), .b(Divisor), .gt(comparator_1_gt), .eq(comparator_1_eq));  // open: lt
  Multiplexer #(.width(8)) multiplexer_2 (
    .in0({Cociente[6:0], 1'b0}), .in1(or_2_out), .out(CocienteOut), .sel(or_3_out));
  Multiplexer #(.width(8)) multiplexer_3 (
    .in0(multiplexer_1_out), .in1(subtractor_1_out), .out(ResiduoOut), .sel(or_3_out));
  or or_3 (or_3_out, comparator_1_gt, comparator_1_eq, Residuo[7]);

  assign DividendoOut = {Dividendo[14:0], 1'b0};
  assign DivisorOut = Divisor;
endmodule
