// Logisim project ALU_v1.circ as structural Verilog
module Sumador8Bits (
  input  [7:0] A,
  input  [7:0] B,
  input  Cin,
  output [7:0] X,
  output C,
  output O,
  output S,
  output Z
);

  wire suma4b_1_c;

  Suma4B suma4b_1 (.A(A[3:0]), .B(B[3:0]), .Cin(Cin), .C(suma4b_1_c), .X(X[3:0]));
  Suma4B suma4b_2 (.A(A[7:4]), .B(B[7:4]), .Cin(suma4b_1_c), .C(C), .X({S, X[6:4]}));
  xor xor_1 (O, X[6], S);
  Comparator comparator_1 (.a({S, X[6:0]}), .b({8{1'b0}}), .eq(Z));  // open: gt, lt

  assign X[7] = S;
endmodule

module Suma1B (
  input  CarryIn,
  input  A,
  input  B,
  output CarryOut,
  output Suma
);

  wire and_1_out, and_2_out, and_3_out, and_4_out, and_5_out, and_6_out, and_7_out, not_1_out, not_2_out,
       not_3_out;

  not not_1 (not_1_out, CarryIn);
  not not_2 (not_2_out, A);
  not not_3 (not_3_out, B);
  and and_1 (and_1_out, A, B);
  and and_2 (and_2_out, CarryIn, B);
  and and_3 (and_3_out, CarryIn, A);
  and and_4 (and_4_out, not_1_out, not_2_out, B);
  and and_5 (and_5_out, not_1_out, A, not_3_out);
  and and_6 (and_6_out, CarryIn, not_2_out, not_3_out);
  and and_7 (and_7_out, CarryIn, A, B);
  or or_1 (CarryOut, and_1_out, and_2_out, and_3_out);
  or or_2 (Suma, and_4_out, and_5_out, and_6_out, and_7_out);
endmodule

module Suma4B (
  input  [3:0] A,
  input  [3:0] B,
  input  Cin,
  output C,
  output [3:0] X
);

  wire suma1b_1_carryout, suma1b_2_carryout, suma1b_3_carryout;

  Suma1B suma1b_1 (.CarryIn(Cin), .A(A[0]), .B(B[0]), .CarryOut(suma1b_1_carryout), .Suma(X[0]));
  Suma1B suma1b_2 (.CarryIn(suma1b_1_carryout), .A(A[1]), .B(B[1]), .CarryOut(suma1b_2_carryout), .Suma(X[1]));
  Suma1B suma1b_3 (.CarryIn(suma1b_2_carryout), .A(A[2]), .B(B[2]), .CarryOut(suma1b_3_carryout), .Suma(X[2]));
  Suma1B suma1b_4 (.CarryIn(suma1b_3_carryout), .A(A[3]), .B(B[3]), .CarryOut(C), .Suma(X[3]));
endmodule

module Resta (
  input  BorrowIn,
  input  A,
  input  B,
  output BorrowOut,
  output Resta
);

  wire and_1_out, and_2_out, and_3_out, and_4_out, and_5_out, and_6_out, and_7_out, not_1_out, not_2_out,
       not_3_out;

  not not_1 (not_1_out, BorrowIn);
  not not_2 (not_2_out, A);
  not not_3 (not_3_out, B);
  and and_1 (and_1_out, not_2_out, B);
  and and_2 (and_2_out, BorrowIn, not_2_out);
  and and_3 (and_3_out, BorrowIn, B);
  and and_4 (and_4_out, not_1_out, not_2_out, B);
  and and_5 (and_5_out, not_1_out, A, not_3_out);
  and and_6 (and_6_out, BorrowIn, not_2_out, not_3_out);
  and and_7 (and_7_out, BorrowIn, A, B);
  or or_1 (BorrowOut, and_1_out, and_2_out, and_3_out);
  or or_2 (Resta, and_4_out, and_5_out, and_6_out, and_7_out);
endmodule

module Resta4B (
  input  [3:0] A,
  input  [3:0] B,
  input  BorrowIn,
  output Borrow,
  output [3:0] X
);

  wire resta_1_borrowout, resta_2_borrowout, resta_3_borrowout;

  Resta resta_1 (.BorrowIn(BorrowIn), .A(A[0]), .B(B[0]), .BorrowOut(resta_1_borrowout), .Resta(X[0]));
  Resta resta_2 (.BorrowIn(resta_1_borrowout), .A(A[1]), .B(B[1]), .BorrowOut(resta_2_borrowout), .Resta(X[1]));
  Resta resta_3 (.BorrowIn(resta_2_borrowout), .A(A[2]), .B(B[2]), .BorrowOut(resta_3_borrowout), .Resta(X[2]));
  Resta resta_4 (.BorrowIn(resta_3_borrowout), .A(A[3]), .B(B[3]), .BorrowOut(Borrow), .Resta(X[3]));
endmodule

module Restador8Bits (
  input  [7:0] A,
  input  [7:0] B,
  input  Cin,
  output [7:0] X,
  output C,
  output O,
  output S,
  output Z
);

  wire resta4b_1_borrow;

  Resta4B resta4b_1 (.A(A[3:0]), .B(B[3:0]), .BorrowIn(Cin), .Borrow(resta4b_1_borrow), .X(X[3:0]));
  Resta4B resta4b_2 (.A(A[7:4]), .B(B[7:4]), .BorrowIn(resta4b_1_borrow), .Borrow(C), .X({S, X[6:4]}));
  nor nor_1 (Z, X[0], X[1], X[2], X[3], X[4], X[5], X[6], S);
  xnor xnor_1 (O, X[6], S);

  assign X[7] = S;
endmodule

module Negador8Bits (
  input  [7:0] N
);

  Adder adder_1 (.a(N), .b({8{1'b1}}));  // open: out, cin, cout
endmodule
