// Logisim project AluMADUROCACHONDO.circ as structural Verilog: 11 circuits, main circuit Alu
module Alu (
  input  [7:0] N,
  input  [7:0] R0,
  input  [7:0] R1,
  input  [3:0] Banderas,
  input  [4:0] Instrucciones,
  output [7:0] ACC,
  output [7:0] ACC2,
  output [3:0] BanderasOut
);

  wire [19:0] add_1_salida, idiv_1_salida, rcl_1_salida, rcr_1_salida, roln_1_salida, rorn_1_salida,
       shl_1_salida, shr_1_salida, xchg_1_salida;

  xchg xchg_1 (.Entrada({Banderas, R1, R0, N}), .Salida(xchg_1_salida));
  add add_1 (.Entrada({Banderas, R1, R0, N}), .Salida(add_1_salida));
  IDIV idiv_1 (.ENTRADA({Banderas, R1, R0, N}), .SALIDA(idiv_1_salida));
  SHL shl_1 (.ENTRADA({Banderas, R1, R0, N}), .SALIDA(shl_1_salida));
  SHR shr_1 (.ENTRADA({Banderas, R1, R0, N}), .SALIDA(shr_1_salida));
  RCL rcl_1 (.Entrada({Banderas, R1, R0, N}), .SALIDA(rcl_1_salida));
  RCR rcr_1 (.Entrada({Banderas, R1, R0, N}), .SALIDA(rcr_1_salida));
  ROLN roln_1 (.ENTRADA({Banderas, R1, R0, N}), .SALIDA(roln_1_salida));
  RORN rorn_1 (.ENTRADA({Banderas, R1, R0, N}), .SALIDA(rorn_1_salida));
  Multiplexer #(.select(5), .width(20)) multiplexer_1 (
    .in0(xchg_1_salida), .in2(add_1_salida), .in6(idiv_1_salida), .in17(shl_1_salida), .in18(shr_1_salida),
    .in19(rcl_1_salida), .in20(rcr_1_salida), .in21(roln_1_salida), .in22(rorn_1_salida),
    .out({BanderasOut, ACC2, ACC}), .sel(Instrucciones));  // open: in1, in3, in4, in5, in7, in8, in9, in10, in11, in12, in13, in14, in15, in16, in23, in24, in25, in26, in27, in28, in29, in30, in31

  // Notes on the sheet:
  //   C O S Z
endmodule

module add (
  input  [27:0] Entrada,
  output [19:0] Salida
);

  wire xnor_1_out, xor_1_out;

  Adder adder_1 (.a(Entrada[7:0]), .b(Entrada[15:8]), .out({Salida[17], Salida[6:0]}), .cin(1'b0), .cout(Salida[19]));
  xor xor_1 (xor_1_out, Salida[17], Entrada[7]);
  xnor xnor_1 (xnor_1_out, Entrada[7], Entrada[15]);
  nor nor_1 (Salida[16], Salida[0], Salida[1], Salida[2], Salida[3], Salida[4], Salida[5], Salida[6], Salida[17]);
  and and_1 (Salida[18], xor_1_out, xnor_1_out);

  assign Salida[15:7] = {Entrada[23:16], Salida[17]};

  // Notes on the sheet:
  //   N
  //   R0
  //   R1
  //   acc
  //   acc2
  //   cosz
endmodule

module xchg (
  input  [27:0] Entrada,
  output [19:0] Salida
);


  assign Salida = {Entrada[27:24], Entrada[15:8], Entrada[23:16]};

  // Notes on the sheet:
  //   N
  //   BANDERAS
  //   R0 -> ACC2
  //   R1 -> ACC
endmodule

module ROLN (
  input  [27:0] ENTRADA,
  output [19:0] SALIDA
);

  Comparator comparator_1 (.a({ENTRADA[6:0], ENTRADA[7]}), .b({8{1'b0}}), .eq(SALIDA[16]));  // open: gt, lt

  assign {SALIDA[19:17], SALIDA[15:0]} = {ENTRADA[7], ENTRADA[26], ENTRADA[6], ENTRADA[23:16], ENTRADA[6:0], ENTRADA[7]};
endmodule

module RORN (
  input  [27:0] ENTRADA,
  output [19:0] SALIDA
);

  Comparator comparator_1 (.a({ENTRADA[0], ENTRADA[7:1]}), .b({8{1'b0}}), .eq(SALIDA[16]));  // open: gt, lt

  assign {SALIDA[19:17], SALIDA[15:0]} = {ENTRADA[0], ENTRADA[26], ENTRADA[0], ENTRADA[23:16], ENTRADA[0], ENTRADA[7:1]};
endmodule

module RCL (
  input  [27:0] Entrada,
  output [19:0] SALIDA
);

  Comparator comparator_1 (.a({Entrada[6:0], Entrada[24]}), .b({8{1'b0}}), .eq(SALIDA[16]));  // open: gt, lt

  assign {SALIDA[19:17], SALIDA[15:0]} = {Entrada[7], Entrada[26], Entrada[6], Entrada[23:16], Entrada[6:0], Entrada[24]};
endmodule

module RCR (
  input  [27:0] Entrada,
  output [19:0] SALIDA
);

  Comparator comparator_1 (.a({Entrada[24], Entrada[7:1]}), .b({8{1'b0}}), .eq(SALIDA[16]));  // open: gt, lt

  assign {SALIDA[19:17], SALIDA[15:0]} = {Entrada[0], Entrada[26], Entrada[24:16], Entrada[24], Entrada[7:1]};
endmodule

module SHL (
  input  [27:0] ENTRADA,
  output [19:0] SALIDA
);

  Comparator comparator_1 (.a({ENTRADA[6:0], 1'b0}), .b({8{1'b0}}), .eq(SALIDA[16]));  // open: gt, lt

  assign {SALIDA[19:17], SALIDA[15:0]} = {ENTRADA[7], ENTRADA[26], ENTRADA[6], ENTRADA[23:16], ENTRADA[6:0], 1'b0};
endmodule

module SHR (
  input  [27:0] ENTRADA,
  output [19:0] SALIDA
);

  Comparator comparator_1 (.a({1'b0, ENTRADA[7:1]}), .b({8{1'b0}}), .eq(SALIDA[16]));  // open: gt, lt

  assign {SALIDA[19:17], SALIDA[15:0]} = {ENTRADA[0], ENTRADA[26], 1'b0, ENTRADA[23:16], 1'b0, ENTRADA[7:1]};
endmodule

module IDIV (
  input  [27:0] ENTRADA,
  output [19:0] SALIDA
);

  div8b div8b_1 (
    .Divisor(ENTRADA[7:0]), .Dividendo(ENTRADA[23:8]), .CocienteOut({SALIDA[17], SALIDA[6:0]}),
    .ResiduoOut(SALIDA[15:8]));  // open: Overflow, Oout, DivisorOut, DividendoOut, Cout, Sout, Zout
  Comparator comparator_1 (.a({SALIDA[17], SALIDA[6:0]}), .b({8{1'b0}}), .eq(SALIDA[16]));  // open: gt, lt

  assign {SALIDA[19:18], SALIDA[7]} = {ENTRADA[27:26], SALIDA[17]};
endmodule

module div8b (
  input  [7:0] Divisor,
  input  [15:0] Dividendo,
  output Overflow,
  output [7:0] CocienteOut,
  output [7:0] ResiduoOut,
  output Oout,
  output [7:0] DivisorOut,
  output [15:0] DividendoOut,
  output Cout,
  output Sout,
  output Zout
);

  wire divicionetapa1_1_p5, divicionetapa1_1_p6, divicionetapa1_1_p7, divicionetapa1_1_p8,
       divicionetapa1_2_p1, divicionetapa1_2_p2, divicionetapa1_2_p3, divicionetapa1_2_p4,
       divicionetapa1_3_p2, divicionetapa1_3_p3, divicionetapa1_3_p4, divicionetapa1_4_p1,
       divicionetapa1_4_p2, divicionetapa1_4_p3, divicionetapa1_4_p4, divicionetapa1_5_p1,
       divicionetapa1_5_p2, divicionetapa1_5_p3, divicionetapa1_5_p4, divicionetapa1_9_p1,
       divicionetapa1_9_p2, divicionetapa1_9_p3, divicionetapa1_9_p4;
  wire [7:0] divicionetapa1_3_p1;

  // divicionEtapa1 divicionetapa1_1: pin names not known; wires that end beside it: {8{1'b0}}, {8{1'b0}}, Divisor, Dividendo, divicionetapa1_1_p5, divicionetapa1_1_p6, divicionetapa1_1_p7, divicionetapa1_1_p8, divicionetapa1_1_p5, divicionetapa1_1_p6, divicionetapa1_1_p7, divicionetapa1_1_p8
  // divicionEtapa1 divicionetapa1_2: pin names not known; wires that end beside it: divicionetapa1_2_p1, divicionetapa1_2_p2, divicionetapa1_2_p3, divicionetapa1_2_p4
  // divicionEtapa1 divicionetapa1_3: pin names not known; wires that end beside it: divicionetapa1_3_p1, divicionetapa1_3_p2, divicionetapa1_3_p3, divicionetapa1_3_p4
  // divicionEtapa1 divicionetapa1_4: pin names not known; wires that end beside it: divicionetapa1_4_p1, divicionetapa1_4_p2, divicionetapa1_4_p3, divicionetapa1_4_p4
  // divicionEtapa1 divicionetapa1_5: pin names not known; wires that end beside it: divicionetapa1_5_p1, divicionetapa1_5_p2, divicionetapa1_5_p3, divicionetapa1_5_p4, divicionetapa1_5_p1, divicionetapa1_5_p2, divicionetapa1_5_p3, divicionetapa1_5_p4
  // divicionEtapa1 divicionetapa1_6: pin names not known
  // divicionEtapa1 divicionetapa1_7: pin names not known
  // divicionEtapa1 divicionetapa1_8: pin names not known
  // divicionEtapa1 divicionetapa1_9: pin names not known; wires that end beside it: divicionetapa1_9_p1, divicionetapa1_9_p2, divicionetapa1_9_p3, divicionetapa1_9_p4, divicionetapa1_9_p1, divicionetapa1_9_p2, divicionetapa1_9_p3, divicionetapa1_9_p4
  // divicionEtapa1 divicionetapa1_10: pin names not known
  // divicionEtapa1 divicionetapa1_11: pin names not known
  // divicionEtapa1 divicionetapa1_12: pin names not known
  // divicionEtapa1 divicionetapa1_13: pin names not known; wires that end beside it: divicionetapa1_3_p1, divicionetapa1_3_p2, divicionetapa1_3_p3, divicionetapa1_3_p4
  // divicionEtapa1 divicionetapa1_14: pin names not known; wires that end beside it: divicionetapa1_4_p1, divicionetapa1_4_p2, divicionetapa1_4_p3, divicionetapa1_4_p4
  // divicionEtapa1 divicionetapa1_15: pin names not known; wires that end beside it: CocienteOut, ResiduoOut, DivisorOut, DividendoOut
  // divicionEtapa1 divicionetapa1_16: pin names not known; wires that end beside it: divicionetapa1_2_p1, divicionetapa1_2_p2, divicionetapa1_2_p3, divicionetapa1_2_p4
  or or_1 (Overflow, divicionetapa1_3_p1[0], divicionetapa1_3_p1[1], divicionetapa1_3_p1[2], divicionetapa1_3_p1[3], divicionetapa1_3_p1[4], divicionetapa1_3_p1[5], divicionetapa1_3_p1[6], divicionetapa1_3_p1[7]);
  nor nor_1 (Cout, DivisorOut[0], DivisorOut[1], DivisorOut[2], DivisorOut[3], DivisorOut[4], DivisorOut[5], DivisorOut[6], DivisorOut[7]);
  nor nor_2 (Zout, CocienteOut[0], CocienteOut[1], CocienteOut[2], CocienteOut[3], CocienteOut[4], CocienteOut[5], CocienteOut[6], CocienteOut[7]);
  or or_2 (Oout, Overflow, Cout);

  assign Sout = CocienteOut[7];
endmodule
