// Logisim project ConvertByteWord.circ as structural Verilog: 1 circuit, main circuit CBW
module CBW (
  input  [27:0] Entrada,
  output [19:0] Salida
);

  NotExactlyOne xnor_1 (
    .out(Salida[16]), .in0(Entrada[8]), .in1(Entrada[8]), .in2(Entrada[9]), .in3(Entrada[10]),
    .in4(Entrada[11]), .in5(Entrada[12]), .in6(Entrada[13]), .in7(Entrada[15]));

  assign {Salida[19:17], Salida[15:0]} = {Entrada[25:24], {2{Entrada[15]}}, Entrada[14:8], Entrada[15:8]};
endmodule
