// Logisim project Decrement.circ as structural Verilog: 1 circuit, main circuit DEC
module DEC (
  input  [27:0] Entrada,
  output [19:0] Salida
);

  wire xnor_1_out, xor_1_out;

  Subtractor subtractor_1 (.a(Entrada[7:0]), .b(8'h1), .out({Salida[17], Salida[6:0]}), .bin(1'b0), .bout(Salida[19]));
  xor xor_1 (xor_1_out, Salida[17], Entrada[7]);
  xnor xnor_1 (xnor_1_out, Entrada[7], 1'b0);
  nor nor_1 (Salida[16], Salida[0], Salida[1], Salida[2], Salida[3], Salida[4], Salida[5], Salida[6], Salida[17]);
  and and_1 (Salida[18], xor_1_out, xnor_1_out);

  assign Salida[15:7] = {Entrada[23:16], Salida[17]};

  // Notes on the sheet:
  //   N
  //   R0
  //   R1
  //   Z
  //   S
  //   O
  //   C
endmodule
