// Logisim project Increment.circ as structural Verilog: 1 circuit, main circuit INC
module INC (
  input  [27:0] Entrada,
  output [19:0] Salida
);

  Adder adder_1 (.a(Entrada[7:0]), .b(8'h1), .out(Salida[7:0]));  // open: cin, cout

  assign Salida[19:8] = Entrada[27:16];

  // Notes on the sheet:
  //   Flags
  //   N
  //   R0
  //   R1
  //   Ya que juntemos todo le ponemos nuestra suma casera
endmodule
