// Logisim project NegadorALU.circ as structural Verilog: 1 circuit, main circuit main
module main (
  input  [27:0] in_1,
  output [19:0] out_2
);

  wire [7:0] adder_1_out;

  assign out_2[7:0] = ~adder_1_out;  // NOT_Gate not_1, 8 bits wide
  Adder adder_1 (.a({8{1'b1}}), .b(in_1[7:0]), .out(adder_1_out), .cout(out_2[17]));  // open: cin
  nor nor_1 (out_2[19], in_1[0], in_1[1], in_1[2], in_1[3], in_1[4], in_1[5], in_1[6], in_1[7]);

  assign {out_2[18], out_2[16:8]} = {in_1[7], in_1[24:16]};

  // Notes on the sheet:
  //   COSZ
endmodule
