// Logisim project NotComparativo.circ as structural Verilog: 1 circuit, main circuit NOT2
module NOT2 (
  input  [27:0] in_1,
  output [19:0] out_2
);

  assign out_2[7:0] = ~in_1[7:0];  // NOT_Gate not_1, 8 bits wide
  nor nor_1 (out_2[19], in_1[0], in_1[1], in_1[2], in_1[3], in_1[4], in_1[5], in_1[6], in_1[7]);

  assign out_2[18:8] = {in_1[7], in_1[25:16]};

  // Notes on the sheet:
  //   COSZ
endmodule
