// Logisim project XorComparativo.circ as structural Verilog: 1 circuit, main circuit XOR2
module XOR2 (
  input  [27:0] Entrada,
  output [19:0] Salida
);

  assign Salida[7:0] = Entrada[7:0] ^ Entrada[15:8];  // XOR_Gate xor_1, 8 bits wide
  nor nor_1 (Salida[19], Entrada[0], Entrada[1], Entrada[2], Entrada[3], Entrada[4], Entrada[5], Entrada[6], Entrada[7]);

  assign Salida[18:8] = {Entrada[7], Entrada[25:16]};
endmodule
